# Fritzing sketch ModeloEsquematico (saved by Fritzing 0.9.3b)
breadboards: 1

parts:
  Componente1 = Arduino Mega ADK (Rev3)
  LCD1 = LCD screen
  Keypad4x1 = Keypad Membran 4x4
  Mod1 = KY-013 Analog Temperature Sensor Module [package="Breakout board"]
  Mod2 = KY-018 Photoresistor Module [package="Breakout board"]
  LED1 = RGB LED - (4 legs) [package="5 mm [THT]"]
  Componente2 = Passive Buzzer
  FC-1 = Sound Sensor
  R1 = Rotary Potentiometer (Large) [maximum_resistance=100kΩ package=THT]

nets:
  N1: Componente1.A0, Mod1.S
  N2: Componente1.A1, Mod2.S
  N3: Componente1.A2, FC-1.OUT
  N4: Componente1.D13_PWM, LED1.blue_cathode
  N5: Componente1.D12_PWM, LED1.green_cathode
  N6: Componente1.D11_PWM, LED1.red_cathode
  N7: Componente1.D10_PWM, Componente2.S
  N8: Componente1.D8_PWM, LCD1.RS
  VIN: Componente1.IOREF, Componente1.5V, LCD1.VDD, LCD1.LED+, Mod1.Vin, Mod2.Vin, Componente2.NC, FC-1.VCC, R1.leg1
  GND: Componente1.GND, LCD1.VSS, LCD1.R/W, LCD1.LED-, Mod1.-, Mod2.-, LED1.common_anode, Componente2.GND, FC-1.GND, R1.leg2
  N9: Componente1.D2_PWM, LCD1.DB7
  N10: Componente1.D3_PWM, LCD1.DB6
  N11: Componente1.D4_PWM, LCD1.DB5
  N12: Componente1.D5_PWM, LCD1.DB4
  N13: Componente1.D7_PWM, LCD1.E
  N14: Componente1.D30, Keypad4x1.Pin1
  N15: Componente1.D31, Keypad4x1.Pin5
  N16: Componente1.D32, Keypad4x1.Pin2
  N17: Componente1.D33, Keypad4x1.Pin6
  N18: Componente1.D34, Keypad4x1.Pin3
  N19: Componente1.D35, Keypad4x1.Pin7
  N20: Componente1.D36, Keypad4x1.Pin4
  N21: Componente1.D37, Keypad4x1.Pin8
  N22: LCD1.V0, R1.wiper

custom parts:
  Keypad Membran 4x4: Membrane Keypad 4x4 Matrix
  KY-013 Analog Temperature Sensor Module: KY-013 Analog Temperature Sensor module, measures ambient temperature based on resistance of the thermistor.
  KY-018 Photoresistor Module: KY-018 Photoresistor module, used to measure light intensity. It can determine the presence or absence of light.
